// Logisim project datapathProject.circ as structural Verilog: 6 circuits, main circuit main
module main (
  input  in_1
);

  wire clock_1_out, clock_2_out, clock_3_out, control_1_store_signal;
  wire [15:0] ALU_output, bit_extender_1_out, Data_Memory_output, multiplexer_1_out, multiplexer_2_out,
       pc_1_out_2, registers_1_read_data_1, registers_1_read_data_2, rom_1_data;

  PC pc_1 (.Clock(clock_1_out), .out_2(pc_1_out_2));
  Clock clock_1 (.out(clock_1_out));
  ROM #(.addrWidth(16), .dataWidth(16)) rom_1 (.addr(pc_1_out_2), .data(rom_1_data), .sel(in_1));
  Clock clock_2 (.out(clock_2_out));
  Clock clock_3 (.out(clock_3_out));
  Control control_1 (.Op_Code(rom_1_data[15:9]), .Store_Signal(control_1_store_signal));  // open: Sub_Signal, Or_Signal
  Registers registers_1 (
    .RegWrite(control_1_store_signal), .Write_Data(multiplexer_2_out), .Clock(clock_2_out),
    .Write_Register(rom_1_data[2:0]), .Read_Reg_1(rom_1_data[8:6]), .Read_Reg_2(rom_1_data[5:3]),
    .Read_Data_1(registers_1_read_data_1), .Read_Data_2(registers_1_read_data_2));
  assign bit_extender_1_out = {{13{rom_1_data[2]}}, rom_1_data[2:0]};  // Bit_Extender bit_extender_1
  Multiplexer #(.width(16)) multiplexer_1 (
    .in0(registers_1_read_data_1), .in1(bit_extender_1_out), .out(multiplexer_1_out),
    .sel(control_1_store_signal));  // open: en
  ALU ALU (
    .FIRST_DATA(multiplexer_1_out), .SECOND_DATA(registers_1_read_data_2), .Op_Code(rom_1_data[15:9]),
    .OUTPUT(ALU_output));
  Data_Memory Data_Memory (
    .Adress(ALU_output), .Data(registers_1_read_data_1), .MemWrite(control_1_store_signal),
    .Clock(clock_3_out), .Output(Data_Memory_output));  // open: MemRead, Clear
  Multiplexer #(.width(16)) multiplexer_2 (
    .in0(ALU_output), .in1(Data_Memory_output), .out(multiplexer_2_out), .sel(control_1_store_signal));  // open: en

  // Notes on the sheet:
  //   Instruction Memory
  //   contents of rom_1 (hex, n*v repeats v):
  //   40a 9 2e5
  //   OPCODE
  //   CONTROL UNIT
endmodule

module ALU (
  input  [15:0] FIRST_DATA,
  input  [15:0] SECOND_DATA,
  input  [6:0] Op_Code,
  output [15:0] OUTPUT
);

  wire [15:0] adder_1_out, OR_out, subtractor_1_out;

  Subtractor #(.width(16)) subtractor_1 (.a(FIRST_DATA), .b(SECOND_DATA), .out(subtractor_1_out));  // open: bin, bout
  assign OR_out = FIRST_DATA | SECOND_DATA;  // OR_Gate OR, 16 bits wide
  Adder #(.width(16)) adder_1 (.a(FIRST_DATA), .b(SECOND_DATA), .out(adder_1_out));  // open: cin, cout
  Multiplexer #(.select(2), .width(16)) multiplexer_1 (
    .in0(adder_1_out), .in1(subtractor_1_out), .in2(OR_out), .out(OUTPUT), .sel(Op_Code[1:0]));  // open: in3, en
endmodule

module Registers (
  input  [2:0] Read_Reg_1,
  input  RegWrite,
  input  [2:0] Write_Register,
  input  [2:0] Read_Reg_2,
  input  [15:0] Write_Data,
  input  Clock,
  output [15:0] Read_Data_1,
  output [15:0] Read_Data_2
);

  wire demultiplexer_1_out0, demultiplexer_1_out1, demultiplexer_1_out2, demultiplexer_1_out3,
       demultiplexer_1_out4, demultiplexer_1_out5, demultiplexer_1_out6, demultiplexer_1_out7, not_1_out;
  wire [15:0] register_1_q, register_2_q, register_3_q, register_4_q, register_5_q, register_6_q,
       register_7_q, register_8_q;

  not not_1 (not_1_out, RegWrite);
  Demultiplexer #(.select(3)) demultiplexer_1 (
    .out0(demultiplexer_1_out0), .out1(demultiplexer_1_out1), .out2(demultiplexer_1_out2),
    .out3(demultiplexer_1_out3), .out4(demultiplexer_1_out4), .out5(demultiplexer_1_out5),
    .out6(demultiplexer_1_out6), .out7(demultiplexer_1_out7), .in(not_1_out), .sel(Write_Register));  // open: en
  Register #(.width(16)) register_1 (
    .D(Write_Data), .en(demultiplexer_1_out0), .Q(register_1_q), .clk(Clock));  // open: clr
  Register #(.width(16)) register_2 (
    .D(Write_Data), .en(demultiplexer_1_out1), .Q(register_2_q), .clk(Clock));  // open: clr
  Register #(.width(16)) register_3 (
    .D(Write_Data), .en(demultiplexer_1_out2), .Q(register_3_q), .clk(Clock));  // open: clr
  Register #(.width(16)) register_4 (
    .D(Write_Data), .en(demultiplexer_1_out3), .Q(register_4_q), .clk(Clock));  // open: clr
  Register #(.width(16)) register_5 (
    .D(Write_Data), .en(demultiplexer_1_out4), .Q(register_5_q), .clk(Clock));  // open: clr
  Register #(.width(16)) register_6 (
    .D(Write_Data), .en(demultiplexer_1_out5), .Q(register_6_q), .clk(Clock));  // open: clr
  Register #(.width(16)) register_7 (
    .D(Write_Data), .en(demultiplexer_1_out6), .Q(register_7_q), .clk(Clock));  // open: clr
  Register #(.width(16)) register_8 (
    .D(Write_Data), .en(demultiplexer_1_out7), .Q(register_8_q), .clk(Clock));  // open: clr
  Multiplexer #(.select(3), .width(16)) multiplexer_1 (
    .in0(register_1_q), .in1(register_2_q), .in2(register_3_q), .in3(register_4_q), .in4(register_5_q),
    .in5(register_6_q), .in6(register_7_q), .in7(register_8_q), .out(Read_Data_1), .sel(Read_Reg_1));  // open: en
  Multiplexer #(.select(3), .width(16)) multiplexer_2 (
    .in0(register_1_q), .in1(register_2_q), .in2(register_3_q), .in3(register_4_q), .in4(register_5_q),
    .in5(register_6_q), .in6(register_7_q), .in7(register_8_q), .out(Read_Data_2), .sel(Read_Reg_2));  // open: en
endmodule

module PC (
  input  Clock,
  output [15:0] out_2
);

  wire [15:0] adder_1_out;

  Register #(.width(16)) PC (.D(adder_1_out), .en(1'b1), .Q(out_2), .clk(Clock));  // open: clr
  Adder #(.width(16)) adder_1 (.a(16'h1), .b(out_2), .out(adder_1_out));  // open: cin, cout
endmodule

module Data_Memory (
  input  [15:0] Adress,
  input  [15:0] Data,
  input  Clock,
  input  MemWrite,
  input  Clear,
  input  MemRead,
  output [15:0] Output
);

  RAM #(.addrWidth(16), .dataWidth(16), .bus("separate")) ram_1 (
    .addr(Adress), .din(Data), .data(Output), .str(MemWrite), .sel(1'b1), .clk(Clock), .ld(MemRead),
    .clr(Clear));
endmodule

module Control (
  input  [6:0] Op_Code,
  output Store_Signal,
  output Sub_Signal,
  output Or_Signal
);

  Demultiplexer #(.select(2)) demultiplexer_1 (
    .out0(Store_Signal), .out1(Sub_Signal), .out2(Or_Signal), .in(1'b1), .sel(Op_Code[1:0]));  // open: out3, en

  // Notes on the sheet:
  //   0--> STR
  //   1 -- SUB
  //   2-- OR
  //   0-2   Memory Instructions ( 3 bit) 
endmodule
